// Logisim project custom_reg.circ as structural Verilog: 12 circuits, main circuit 1bit_reg
module _1bit_reg (
  input  Clock,
  input  Data,
  input  Clear,
  input  Load,
  output Data_out
);

  wire and_1_out, and_2_out, not_1_out, not_2_out;

  and and_1 (and_1_out, Data, Load);
  not not_1 (not_1_out, Data);
  and and_2 (and_2_out, not_1_out, Load);
  J_K_Flip_Flop j_k_ff_1 (
    .J(and_1_out), .clk(Clock), .K(and_2_out), .Q(Data_out), .preset(1'b0), .en(not_2_out), .reset(Clear));  // open: Qn
  not not_2 (not_2_out, Clear);

  // Notes on the sheet:
  //   Raymond Green
  //   OLA 5
  //   1 Bit Register Circuit
endmodule

module Register (
  input  [31:0] Data_In,
  input  Clock,
  input  Load,
  output [31:0] Data_Out
);

  Register_part #(.width(32)) register_1 (.D(Data_In), .en(Load), .Q(Data_Out), .clk(Clock));  // open: clr

  // Notes on the sheet:
  //   Raymond Green
  //   OLA 5
  //   Register Circuit
endmodule

module BusRegister (
  input  Clock,
  input  [31:0] Data_In,
  input  Load,
  input  Bus,
  output [31:0] Data_Out,
  output [31:0] Bus_Out
);

  Register_part #(.width(32)) register_1 (.D(Data_In), .en(Load), .Q(Data_Out), .clk(Clock));  // open: clr
  assign Bus_Out = Bus ? Data_Out : 32'bz;  // Controlled_Buffer controlled_buffer_1

  // Notes on the sheet:
  //   Raymond Green
  //   OLA 5
  //   Bus Register Circuit
endmodule

module ClearRegister (
  input  Clock,
  input  [31:0] Data_In,
  input  Load,
  input  Clear,
  input  Bus,
  output [31:0] Data_Out,
  output [31:0] Bus_Out
);

  Register_part #(.width(32)) register_1 (.D(Data_In), .en(Load), .Q(Data_Out), .clk(Clock), .clr(Clear));
  assign Bus_Out = Bus ? Data_Out : 32'bz;  // Controlled_Buffer controlled_buffer_1

  // Notes on the sheet:
  //   Raymond Green
  //   OLA 5
  //   Clear Register Circuit
endmodule

module CountRegister (
  input  Clock,
  input  [31:0] Data_In,
  input  Bus,
  input  Count,
  input  Load,
  output [31:0] Data_Out,
  output [31:0] Bus_Out
);

  wire or_1_out;
  wire [31:0] adder_1_out, multiplexer_1_out;

  Adder #(.width(32)) adder_1 (.a(Data_Out), .b(32'h1), .out(adder_1_out));  // open: cin, cout
  Multiplexer #(.width(32), .enable("false")) multiplexer_1 (
    .in0(Data_In), .in1(adder_1_out), .out(multiplexer_1_out), .sel(Count));
  or or_1 (or_1_out, Count, Load);
  Register_part #(.width(32)) register_1 (
    .D(multiplexer_1_out), .en(or_1_out), .Q(Data_Out), .clk(Clock));  // open: clr
  assign Bus_Out = Bus ? Data_Out : 32'bz;  // Controlled_Buffer controlled_buffer_1

  // Notes on the sheet:
  //   Raymond Green
  //   OLA 5
  //   Count Register Circuit
endmodule

module ACC (
  input  Clock,
  input  [31:0] Input,
  input  Load,
  input  Clear,
  input  Bus,
  output [31:0] Output,
  output [31:0] Bus_Out
);

  ClearRegister clearregister_1 (
    .Data_In(Input), .Clock(Clock), .Load(Load), .Clear(Clear), .Bus(Bus), .Data_Out(Output),
    .Bus_Out(Bus_Out));

  // Notes on the sheet:
  //   Raymond Green
  //   OLA 5
  //   ACC Circuit
endmodule

module AR (
  input  Clock,
  input  [31:0] Input,
  input  Load,
  output [31:0] Output
);

  Register register_1 (.Data_In(Input), .Clock(Clock), .Load(Load), .Data_Out(Output));

  // Notes on the sheet:
  //   Raymond Green
  //   OLA 5
  //   AR Circuit
endmodule

module DR (
  input  Clock,
  input  [31:0] Input,
  input  Load,
  input  Bus,
  output [31:0] Output,
  output [31:0] Bus_Out
);

  BusRegister busregister_1 (
    .Data_In(Input), .Clock(Clock), .Load(Load), .Bus(Bus), .Data_Out(Output), .Bus_Out(Bus_Out));

  // Notes on the sheet:
  //   Raymond Green
  //   OLA 5
  //   DR Circuit
endmodule

module IR (
  input  Clock,
  input  [31:0] Input,
  input  Load,
  output [31:0] Output
);

  Register register_1 (.Data_In(Input), .Clock(Clock), .Load(Load), .Data_Out(Output));

  // Notes on the sheet:
  //   Raymond Green
  //   OLA 5
  //   IR Circuit
endmodule

module OUTR (
  input  Clock,
  input  [31:0] Input,
  input  Load,
  output [31:0] Output
);

  Register register_1 (.Data_In(Input), .Clock(Clock), .Load(Load), .Data_Out(Output));

  // Notes on the sheet:
  //   Raymond Green
  //   OLA 5
  //   OUTR Circuit
endmodule

module PC (
  input  Clock,
  input  [31:0] Input,
  input  Count,
  input  Load,
  input  Bus,
  output [31:0] Output,
  output [31:0] Bus_Out
);

  CountRegister countregister_1 (
    .Data_In(Input), .Clock(Clock), .Count(Count), .Load(Load), .Bus(Bus), .Data_Out(Output));  // open: Bus_Out
  assign Bus_Out = Bus ? Output : 32'bz;  // Controlled_Buffer controlled_buffer_1

  // Notes on the sheet:
  //   Raymond Green
  //   OLA 5
  //   PC Circuit
endmodule

module R (
  input  Clock,
  input  [31:0] Input,
  input  Load,
  input  Bus,
  output [31:0] Output,
  output [31:0] Bus_Out
);

  BusRegister busregister_1 (
    .Data_In(Input), .Clock(Clock), .Load(Load), .Bus(Bus), .Data_Out(Output), .Bus_Out(Bus_Out));

  // Notes on the sheet:
  //   Raymond Green
  //   OLA 5
  //   R Circuit
endmodule
